// Digital circuit Circuito.dig as structural Verilog
module Circuito (
  input  B3,
  input  B2,
  input  B1,
  input  B0,
  input  A3,
  input  A2,
  input  A1,
  input  A0,
  input  O0,
  input  O1,
  input  A4,
  input  A5,
  input  B4,
  input  B5,
  output F,
  output S0,
  output S1,
  output S2,
  output S3,
  output S4,
  output S5,
  output S6,
  output S7
);

  wire comparador_1_s0, comparador_1_s1, comparador_1_s2, comparador_1_s3, comparador_1_s4, comparador_1_s5,
       multiplicador_1_f, multiplicador_1_s0, multiplicador_1_s1, multiplicador_1_s2, multiplicador_1_s3,
       multiplicador_1_s4, multiplicador_1_s5, multiplicador_1_s6, multiplicador_1_s7, somador_1_f,
       somador_1_s0, somador_1_s1, somador_1_s2, somador_1_s3, somador_1_s4, somador_1_s5, subtracao_1_f,
       subtracao_1_s0, subtracao_1_s1, subtracao_1_s2, subtracao_1_s3, subtracao_1_s4, subtracao_1_s5;

  Multiplicador multiplicador_1 (
    .B0(B0), .B1(B1), .B2(B2), .B3(B3), .A0(A0), .A1(A1), .A2(A2), .B4(B4), .B5(B5), .A4(A4), .A5(A5),
    .A3(A3), .F(multiplicador_1_f), .S0(multiplicador_1_s0), .S1(multiplicador_1_s1),
    .S2(multiplicador_1_s2), .S3(multiplicador_1_s3), .S4(multiplicador_1_s4), .S5(multiplicador_1_s5),
    .S6(multiplicador_1_s6), .S7(multiplicador_1_s7));
  Comparador comparador_1 (
    .A0(A0), .A1(A1), .A3(A3), .A2(A2), .A4(A4), .A5(A5), .B0(B0), .B1(B1), .B2(B2), .B3(B3), .B4(B4),
    .B5(B5), .S0(comparador_1_s0), .S1(comparador_1_s1), .S2(comparador_1_s2), .S3(comparador_1_s3),
    .S4(comparador_1_s4), .S5(comparador_1_s5));
  MUX_geral mux_geral_1 (
    .S0_soma(somador_1_s0), .S0_sub(subtracao_1_s0), .S0_comp(comparador_1_s0), .S0_mult(multiplicador_1_s0),
    .S1_soma(somador_1_s1), .S1_sub(subtracao_1_s1), .S1_comp(comparador_1_s2), .S1_mult(multiplicador_1_s1),
    .S2_mult(multiplicador_1_s2), .S2_comp(comparador_1_s1), .S2_sub(subtracao_1_s2), .S2_soma(somador_1_s2),
    .S3_soma(somador_1_s3), .S3_sub(subtracao_1_s3), .S3_comp(comparador_1_s3), .S3_mult(multiplicador_1_s3),
    .S4_soma(somador_1_s4), .S4_sub(subtracao_1_s4), .S4_comp(comparador_1_s4), .S4_mult(multiplicador_1_s4),
    .S5_soma(somador_1_s5), .S5_sub(subtracao_1_s5), .S5_comp(comparador_1_s5), .S5_mult(multiplicador_1_s5),
    .O0(O0), .O1(O1), .S6_mult(multiplicador_1_s6), .S7_mult(multiplicador_1_s7), .F_mult(multiplicador_1_f),
    .F_soma(somador_1_f), .F_sub(subtracao_1_f), .S0(S0), .S1(S1), .S2(S2), .S3(S3), .S4(S4), .S5(S5),
    .S6(S6), .S7(S7), .F(F));
  Somador somador_1 (
    .A0(A0), .A1(A1), .A2(A2), .A3(A3), .A4(A4), .A5(A5), .B0(B0), .B1(B1), .B2(B2), .B3(B3), .B4(B4),
    .B5(B5), .S0(somador_1_s0), .S1(somador_1_s1), .S2(somador_1_s2), .S3(somador_1_s3), .S4(somador_1_s4),
    .S5(somador_1_s5), .F(somador_1_f));
  Subtracao subtracao_1 (
    .A0(A0), .A1(A1), .A2(A2), .A3(A3), .A4(A4), .A5(A5), .B0(B0), .B1(B1), .B2(B2), .B3(B3), .B4(B4),
    .B5(B5), .S0(subtracao_1_s0), .S1(subtracao_1_s1), .S2(subtracao_1_s2), .S3(subtracao_1_s3),
    .S4(subtracao_1_s4), .S5(subtracao_1_s5), .F(subtracao_1_f));
endmodule
