// Digital circuit Comparador.dig as structural Verilog
module Comparador (
  input  A0,
  input  A1,
  input  A3,
  input  A2,
  input  A4,
  input  A5,
  input  B0,
  input  B1,
  input  B2,
  input  B3,
  input  B4,
  input  B5,
  output S0,
  output S1,
  output S2,
  output S3,
  output S4,
  output S5
);

  wire and_2_out, and_3_out, and_4_out, and_5_out, not_1_out, xnor_1_out, xnor_2_out, xnor_3_out, xnor_4_out,
       xnor_5_out, xnor_6_out;

  xnor xnor_1 (xnor_1_out, A0, B0);
  xnor xnor_2 (xnor_2_out, A1, B1);
  and and_1 (S1, not_1_out, A0);
  not not_1 (not_1_out, A0);
  xnor xnor_3 (xnor_3_out, A2, B2);
  xnor xnor_4 (xnor_4_out, A3, B3);
  xnor xnor_5 (xnor_5_out, A4, B4);
  xnor xnor_6 (xnor_6_out, A5, B5);
  and and_2 (and_2_out, xnor_1_out, xnor_2_out);
  and and_3 (and_3_out, xnor_3_out, xnor_4_out);
  and and_4 (and_4_out, xnor_5_out, xnor_6_out);
  and and_5 (and_5_out, and_2_out, and_3_out);
  and and_6 (S0, and_5_out, and_4_out);

  assign S2 = S1;
  assign S3 = S1;
  assign S4 = S1;
  assign S5 = S1;
endmodule
