// Digital circuit Complemento_de_2_certo.dig as structural Verilog
module Complemento_de_2_certo (
  input  B0,
  input  B1,
  input  B2,
  input  B3,
  input  B4,
  input  B5,
  output B0C,
  output B1C,
  output B2C,
  output B3C,
  output B4C,
  output B5C
);

  wire halfadder_1_cout, halfadder_2_cout, halfadder_3_cout, halfadder_4_cout, halfadder_5_cout, not_1_out,
       not_2_out, not_3_out, not_4_out, not_5_out, not_6_out;

  not not_1 (not_1_out, B0);
  not not_2 (not_2_out, B1);
  not not_3 (not_3_out, B2);
  not not_4 (not_4_out, B3);
  not not_5 (not_5_out, B4);
  not not_6 (not_6_out, B5);
  HalfAdder halfadder_1 (.A(1'b1), .B(not_1_out), .S(B0C), .Cout(halfadder_1_cout));
  HalfAdder halfadder_2 (.A(not_2_out), .B(halfadder_1_cout), .S(B1C), .Cout(halfadder_2_cout));
  HalfAdder halfadder_3 (.A(not_3_out), .B(halfadder_2_cout), .S(B2C), .Cout(halfadder_3_cout));
  HalfAdder halfadder_4 (.A(not_4_out), .B(halfadder_3_cout), .S(B3C), .Cout(halfadder_4_cout));
  HalfAdder halfadder_5 (.A(not_5_out), .B(halfadder_4_cout), .S(B4C), .Cout(halfadder_5_cout));
  HalfAdder halfadder_6 (.A(not_6_out), .B(halfadder_5_cout), .S(B5C));  // open: Cout
endmodule
