// Digital circuit MUX_bits_exclusivos_multiplicacao.dig as structural Verilog
module MUX_bits_exclusivos_multiplicacao (
  input  O0,
  input  O1,
  input  S_multi,
  output S__6_ou_7
);

  and and_1 (S__6_ou_7, O1, O0, S_multi);
endmodule
