// Digital circuit MUX_geral.dig as structural Verilog
module MUX_geral (
  input  S0_soma,
  input  S0_sub,
  input  S0_comp,
  input  S0_mult,
  input  S1_soma,
  input  S1_sub,
  input  S1_comp,
  input  S1_mult,
  input  S2_mult,
  input  S2_comp,
  input  S2_sub,
  input  S2_soma,
  input  S3_soma,
  input  S3_sub,
  input  S3_comp,
  input  S3_mult,
  input  S4_soma,
  input  S4_sub,
  input  S4_comp,
  input  S4_mult,
  input  S5_soma,
  input  S5_sub,
  input  S5_comp,
  input  S5_mult,
  input  O0,
  input  O1,
  input  S6_mult,
  input  S7_mult,
  input  F_mult,
  input  F_soma,
  input  F_sub,
  output S0,
  output S1,
  output S2,
  output S3,
  output S4,
  output S5,
  output S6,
  output S7,
  output F
);

  MUX_overflow mux_overflow_1 (.O0(O0), .O1(O1), .Sub(F_sub), .Soma(F_soma), .Mult(F_mult), .F(F));
  MUX_bits_exclusivos_multiplicacao mux_bits_exclusivos_multiplicacao_1 (
    .O0(O0), .O1(O1), .S_multi(S7_mult), .S__6_ou_7(S7));
  MUX_bits_exclusivos_multiplicacao mux_bits_exclusivos_multiplicacao_2 (
    .O0(O0), .O1(O1), .S_multi(S6_mult), .S__6_ou_7(S6));
  MUX_operacao mux_operacao_1 (.Soma(S5_soma), .Sub(S5_sub), .Comp(S5_comp), .Mult(S5_mult), .O0(O0), .O1(O1), .S(S5));
  MUX_operacao mux_operacao_2 (.Soma(S4_soma), .Sub(S4_sub), .Comp(S4_comp), .Mult(S4_mult), .O0(O0), .O1(O1), .S(S4));
  MUX_operacao mux_operacao_3 (.Soma(S3_soma), .Sub(S3_sub), .Comp(S3_comp), .Mult(S3_mult), .O0(O0), .O1(O1), .S(S3));
  MUX_operacao mux_operacao_4 (.Soma(S2_soma), .Sub(S2_sub), .Comp(S2_comp), .Mult(S2_mult), .O0(O0), .O1(O1), .S(S2));
  MUX_operacao mux_operacao_5 (.Soma(S1_soma), .Sub(S1_sub), .Comp(S1_comp), .Mult(S1_mult), .O0(O0), .O1(O1), .S(S1));
  MUX_operacao mux_operacao_6 (.Soma(S0_soma), .Sub(S0_sub), .Comp(S0_comp), .Mult(S0_mult), .O0(O0), .O1(O1), .S(S0));
endmodule
