// Digital circuit MUX_operacao.dig as structural Verilog
module MUX_operacao (
  input  Soma,
  input  Sub,
  input  Comp,
  input  Mult,
  input  O0,
  input  O1,
  output S
);

  wire and_1_out, and_2_out, and_3_out, and_4_out, not_1_out, not_2_out, not_3_out, not_4_out, or_1_out,
       or_2_out;

  not not_1 (not_1_out, O1);
  not not_2 (not_2_out, O0);
  not not_3 (not_3_out, O0);
  not not_4 (not_4_out, O1);
  and and_1 (and_1_out, Soma, not_1_out, not_2_out);
  and and_2 (and_2_out, Comp, O1, not_3_out);
  and and_3 (and_3_out, Sub, not_4_out, O0);
  and and_4 (and_4_out, Mult, O1, O0);
  or or_1 (or_1_out, and_1_out, and_2_out);
  or or_2 (or_2_out, and_3_out, and_4_out);
  or or_3 (S, or_1_out, or_2_out);
endmodule
