// Digital circuit Multiplicador.dig as structural Verilog
module Multiplicador (
  input  B0,
  input  B1,
  input  B2,
  input  B3,
  input  A0,
  input  A1,
  input  A2,
  input  B4,
  input  B5,
  input  A4,
  input  A5,
  input  A3,
  output F,
  output S0,
  output S1,
  output S2,
  output S3,
  output S4,
  output S5,
  output S6,
  output S7
);

  wire and_2_out, and_3_out, and_4_out, and_5_out, and_6_out, and_7_out, and_8_out, and_9_out, and_10_out,
       and_11_out, and_12_out, and_13_out, and_14_out, and_15_out, and_16_out, fulladder_1_cout,
       fulladder_1_s, fulladder_2_cout, fulladder_2_s, fulladder_3_cout, fulladder_3_s, fulladder_4_cout,
       fulladder_4_s, fulladder_5_cout, fulladder_5_s, fulladder_6_cout, fulladder_7_cout, halfadder_1_cout,
       halfadder_2_cout, halfadder_3_cout, halfadder_3_s, halfadder_4_cout;

  // Overflow_Multiplicação overflow_multiplicação_1: pin names not known; wires that end beside it: A4, A5, B4, B5, F
  and and_1 (S0, B0, A0);
  and and_2 (and_2_out, B1, A0);
  and and_3 (and_3_out, B0, A1);
  and and_4 (and_4_out, B2, A0);
  and and_5 (and_5_out, B1, A1);
  and and_6 (and_6_out, B3, A0);
  and and_7 (and_7_out, B2, A1);
  and and_8 (and_8_out, B3, A1);
  and and_9 (and_9_out, B3, A2);
  and and_10 (and_10_out, B3, A3);
  HalfAdder halfadder_1 (.A(and_2_out), .B(and_3_out), .S(S1), .Cout(halfadder_1_cout));
  FullAdder fulladder_1 (
    .A(and_4_out), .B(and_5_out), .Cin(halfadder_1_cout), .S(fulladder_1_s), .Cout(fulladder_1_cout));
  and and_11 (and_11_out, B0, A2);
  FullAdder fulladder_2 (
    .A(and_6_out), .B(and_7_out), .Cin(fulladder_1_cout), .S(fulladder_2_s), .Cout(fulladder_2_cout));
  HalfAdder halfadder_2 (.A(fulladder_1_s), .B(and_11_out), .S(S2), .Cout(halfadder_2_cout));
  and and_12 (and_12_out, B1, A2);
  HalfAdder halfadder_3 (.A(and_8_out), .B(fulladder_2_cout), .S(halfadder_3_s), .Cout(halfadder_3_cout));
  FullAdder fulladder_3 (
    .A(fulladder_2_s), .B(and_12_out), .Cin(halfadder_2_cout), .S(fulladder_3_s), .Cout(fulladder_3_cout));
  and and_13 (and_13_out, B2, A2);
  FullAdder fulladder_4 (
    .A(halfadder_3_cout), .B(and_9_out), .Cin(fulladder_5_cout), .S(fulladder_4_s), .Cout(fulladder_4_cout));
  and and_14 (and_14_out, B0, A3);
  FullAdder fulladder_5 (
    .A(halfadder_3_s), .B(and_13_out), .Cin(fulladder_3_cout), .S(fulladder_5_s), .Cout(fulladder_5_cout));
  HalfAdder halfadder_4 (.A(fulladder_3_s), .B(and_14_out), .S(S3), .Cout(halfadder_4_cout));
  and and_15 (and_15_out, B1, A3);
  and and_16 (and_16_out, B2, A3);
  FullAdder fulladder_6 (.A(fulladder_4_s), .B(and_16_out), .Cin(fulladder_7_cout), .S(S5), .Cout(fulladder_6_cout));
  FullAdder fulladder_7 (.A(fulladder_5_s), .B(and_15_out), .Cin(halfadder_4_cout), .S(S4), .Cout(fulladder_7_cout));
  FullAdder fulladder_8 (.A(fulladder_4_cout), .B(and_10_out), .Cin(fulladder_6_cout), .S(S6), .Cout(S7));
endmodule
