// Digital circuit Overflow_Multiplicação.dig as structural Verilog
module Overflow_Multiplicac_a_o (
  input  A4,
  input  A5,
  input  B4,
  input  B5,
  output F
);

  wire or_1_out, or_2_out;

  or or_1 (or_1_out, A4, B4);
  or or_2 (or_2_out, A5, B5);
  or or_3 (F, or_1_out, or_2_out);
endmodule
