// Digital circuit Overflow_somador.dig as structural Verilog
module Overflow_somador (
  input  S5,
  input  A5,
  input  B5,
  output F
);

  wire and_1_out, and_2_out;

  and and_1 (and_1_out, A5, B5, ~S5);  // And
  and and_2 (and_2_out, ~A5, ~B5, S5);  // And
  or or_1 (F, and_1_out, and_2_out);
endmodule
