// Digital circuit Somador.dig as structural Verilog
module Somador (
  input  A0,
  input  A1,
  input  A2,
  input  A3,
  input  A4,
  input  A5,
  input  B0,
  input  B1,
  input  B2,
  input  B3,
  input  B4,
  input  B5,
  output S0,
  output S1,
  output S2,
  output S3,
  output S4,
  output S5,
  output F
);

  wire fulladder_1_cout, fulladder_2_cout, fulladder_3_cout, fulladder_4_cout, halfadder_1_cout;

  HalfAdder halfadder_1 (.A(B0), .B(A0), .S(S0), .Cout(halfadder_1_cout));
  FullAdder fulladder_1 (.A(A1), .B(B1), .Cin(halfadder_1_cout), .S(S1), .Cout(fulladder_1_cout));
  FullAdder fulladder_2 (.A(A2), .B(B2), .Cin(fulladder_1_cout), .S(S2), .Cout(fulladder_2_cout));
  FullAdder fulladder_3 (.A(A3), .B(B3), .Cin(fulladder_2_cout), .S(S3), .Cout(fulladder_3_cout));
  FullAdder fulladder_4 (.A(A4), .B(B4), .Cin(fulladder_3_cout), .S(S4), .Cout(fulladder_4_cout));
  FullAdder fulladder_5 (.A(A5), .B(B5), .Cin(fulladder_4_cout), .S(S5));  // open: Cout
  Overflow_somador overflow_somador_1 (.S5(S5), .A5(A5), .B5(B5), .F(F));
endmodule
