// Digital circuit Subtracao.dig as structural Verilog
module Subtracao (
  input  A0,
  input  A1,
  input  A2,
  input  A3,
  input  A4,
  input  A5,
  input  B0,
  input  B1,
  input  B2,
  input  B3,
  input  B4,
  input  B5,
  output S0,
  output S1,
  output S2,
  output S3,
  output S4,
  output S5,
  output F
);

  wire complemento_de_2_certo_1_b0c, complemento_de_2_certo_1_b1c, complemento_de_2_certo_1_b2c,
       complemento_de_2_certo_1_b3c, complemento_de_2_certo_1_b4c, complemento_de_2_certo_1_b5c,
       fulladder_1_cout, fulladder_2_cout, fulladder_3_cout, fulladder_4_cout, halfadder_1_cout;

  Complemento_de_2_certo complemento_de_2_certo_1 (
    .B0(B0), .B1(B1), .B2(B2), .B3(B3), .B4(B4), .B5(B5), .B0C(complemento_de_2_certo_1_b0c),
    .B1C(complemento_de_2_certo_1_b1c), .B2C(complemento_de_2_certo_1_b2c),
    .B3C(complemento_de_2_certo_1_b3c), .B4C(complemento_de_2_certo_1_b4c), .B5C(complemento_de_2_certo_1_b5c));
  HalfAdder halfadder_1 (.A(A0), .B(complemento_de_2_certo_1_b0c), .S(S0), .Cout(halfadder_1_cout));
  FullAdder fulladder_1 (
    .A(A1), .B(complemento_de_2_certo_1_b1c), .Cin(halfadder_1_cout), .S(S1), .Cout(fulladder_1_cout));
  FullAdder fulladder_2 (
    .A(A2), .B(complemento_de_2_certo_1_b2c), .Cin(fulladder_1_cout), .S(S2), .Cout(fulladder_2_cout));
  FullAdder fulladder_3 (
    .A(A3), .B(complemento_de_2_certo_1_b3c), .Cin(fulladder_2_cout), .S(S3), .Cout(fulladder_3_cout));
  FullAdder fulladder_4 (
    .A(A4), .B(complemento_de_2_certo_1_b4c), .Cin(fulladder_3_cout), .S(S4), .Cout(fulladder_4_cout));
  FullAdder fulladder_5 (.A(A5), .B(complemento_de_2_certo_1_b5c), .Cin(fulladder_4_cout), .S(S5));  // open: Cout
  // OverflowSubtracao overflowsubtracao_1: pin names not known; wires that end beside it: A5, S5, complemento_de_2_certo_1_b5c, F
endmodule
